# Fritzing sketch breadboard (saved by Fritzing 0.7.10b)
breadboards: 1

parts:
  R1 = Photocell (LDR) [package=THT]
  Arduino1 = Arduino
  J1 = Infrared Proximity Sensor
  Q1 = PHOTOTRANSISTOR REFLECTIVE OBJECT SENSOR [package=qrb1114-side]  # not connected
  T1 = LM35 Temperature Sensor [package="TO92 [THT]"]
  U1 = POT_SWITCH [package=pot_pth]  # not connected
  R2 = Rotary Potentiometer (Small) [maximum_resistance=100kΩ]
  R3 = 10k Ω Resistor [package=THT]

nets:
  GND: R1.pin_0, Arduino1.GND, J1.GND, T1.GND, R2.leg2
  N1: R1.pin_1, Arduino1.A2, R3.Pin_0
  +5V: Arduino1.+5V, J1.Vcc, T1.+Vs, R2.leg1, R3.Pin_1
  N2: Arduino1.A0, R2.wiper
  N3: Arduino1.A1, T1.Vout
  N4: Arduino1.A3, J1.Vout
